# Fritzing sketch I2C (saved by Fritzing 0.9.3b)
breadboards: 1

parts:
  Composant2 = LCD1602-I2C
  A1 = AHT10 module
  Raspberry_Pi_1 = Raspberry Pi 4 [part_number=RPI-4-b]
  M1 = STM32407VG Discovery  # not connected

nets:
  N1: Composant2.GND, A1.Pin_3
  N2: Composant2.VCC, A1.Pin_4
  N3: Composant2.SCL, Raspberry_Pi_1.GPIO3

custom parts:
  LCD1602-I2C: A standard character display, usually with 2x16 characters. Comes in many colors with LCM1602 IIC attached.
  AHT10 module: AHT10 Temperature Humidity Sensor Measurement Module High-Precision Digital Temp Humidity Sensor Measurement Module 1.8-6.0V I2C.
  Raspberry Pi 4: The RPi4, a faster version of the awesome Raspberry Pi 2 B ARM Board with 40 pin gpio. Ready for special Raspberry Pi B+ and RPi2 Hat (Hardware attached (on) top)
  STM32407VG Discovery: The STM32F4DISCOVERY Discovery kit allows users to easily develop applications with the STM32F407VG high performance microcontroller with the ARM® Cortex®-M4 32-bit core. It includes everything required either for beginners or for experienced users to get quickly started.Based on STM32F407VG, it includes an ST-LINK/V2 or ST-LINK/V2-A embedded debug tool, two ST-MEMS digital accelerometers, a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
